# Fritzing sketch Environment Sensor (saved by Fritzing 0.7.4b)
breadboards: 2

parts:
  Teensy1 = Teensy 2.0
  LCD1 = LCD screen
  R1 = Trimmer Potentiometer [maximum_resistance=10kΩ package=THT]
  LPG_Gas = Gas Sensor Breakout Board
  Methane_Gas = Gas Sensor Breakout Board
  CO_Gas = Gas Sensor Breakout Board
  S1 = Pushbutton [package="[THT]"]
  S2 = Pushbutton [package="[THT]"]
  S3 = Pushbutton [package="[THT]"]
  S4 = Pushbutton [package="[THT]"]
  J1 = Piezo Speaker
  R2 = Resistor [tolerance=±5% resistance=10k package=THT]
  R3 = Resistor [tolerance=±5% resistance=10k package=THT]
  R4 = Resistor [tolerance=±5% resistance=10k package=THT]
  R5 = Resistor [tolerance=±5% resistance=10k package=THT]
  R6 = Photocell (LDR) [package=THT]
  T1 = TMP36 Temperature Sensor [package="TO92 [THT]"]
  HF_RFID_Module_SL018_(Stand_In) = Audio Jack Breakout

nets:
  GND: Teensy1.GND, LCD1.VSS, LCD1.R/W, LCD1.LED-, R1.leg1, LPG_Gas.H1, LPG_Gas.GND, Methane_Gas.H1, Methane_Gas.GND, CO_Gas.H1, CO_Gas.GND, S1.Pin_1, S1.Pin_2, S2.Pin_1, S2.Pin_2, S3.Pin_1, S3.Pin_2, S4.Pin_1, S4.Pin_2, J1.pin1, R2.Pin_0, R3.Pin_0, R4.Pin_0, R5.Pin_1, R6.pin_0, T1.+Vs, T1.GND, HF_RFID_Module_SL018_(Stand_In).GND, HF_RFID_Module_SL018_(Stand_In).RING_SHUNT
  N1: Teensy1.B0, LCD1.RS
  N2: Teensy1.B1, LCD1.E
  N3: Teensy1.B2, LCD1.DB4
  N4: Teensy1.B3, LCD1.DB5
  N5: Teensy1.B7, LCD1.DB6
  N6: Teensy1.D0, HF_RFID_Module_SL018_(Stand_In).RING
  N7: Teensy1.D1, HF_RFID_Module_SL018_(Stand_In).TIP_SHUNT
  N8: Teensy1.D2, LCD1.DB7
  N9: Teensy1.D3, S1.Pin_3, S1.Pin_4
  N10: Teensy1.C6, S2.Pin_3, S2.Pin_4
  VCC: Teensy1.VCC, LCD1.VDD, LCD1.LED+, R1.leg2
  N11: Teensy1.D7, J1.pin2
  N12: Teensy1.B4, S3.Pin_3, S3.Pin_4
  N13: Teensy1.B5, S4.Pin_3, S4.Pin_4
  N14: Teensy1.F7, T1.Vout
  N15: Teensy1.F6, R5.Pin_0, R6.pin_1
  N16: Teensy1.F5, CO_Gas.A1
  N17: Teensy1.F4, Methane_Gas.A1
  N18: Teensy1.F1, LPG_Gas.A1
  N19: Teensy1.F0, HF_RFID_Module_SL018_(Stand_In).TIP
  N20: LCD1.V0, R1.wiper
  N21: LPG_Gas.B1, R2.Pin_1
  N22: Methane_Gas.B1, R3.Pin_1
  N23: CO_Gas.B1, R4.Pin_1
